# Fritzing sketch DRAM_interface (saved by Fritzing 0.9.3b)
breadboards: 1

parts:
  Part1 = Arduino Uno (Rev3)
  IC1 = IC, DIP package, 16 pins [chip_label=HM50256-15]

nets:
  N1: Part1.A0, IC1.pin13
  N2: Part1.A1, IC1.pin9
  N3: Part1.A2, IC1.pin1
  N4: Part1.D9_PWM, IC1.pin2
  N5: Part1.D10_PWM/SS, IC1.pin14
  N6: Part1.D11_PWM/MOSI, IC1.pin3
  N7: Part1.D12/MISO, IC1.pin15
  N8: Part1.D13/SCK, IC1.pin4
  N9: Part1.D2, IC1.pin5
  N10: Part1.D3_PWM, IC1.pin7
  N11: Part1.D4, IC1.pin6
  N12: Part1.D5_PWM, IC1.pin12
  N13: Part1.D6_PWM, IC1.pin11
  N14: Part1.D7, IC1.pin10
  N15: Part1.5V, IC1.pin8
  N16: Part1.GND, IC1.pin16

notes:
  Orange - Data I/O
  Green - Control Lines
  Blue - Address Lines
  Red - +5V
  Black - GND
